# Fritzing sketch circuit_peltier_&_sensors (saved by Fritzing 0.9.3b)
breadboards: 2

parts:
  パーツ1 = Arduino Uno (Rev3)
  J1 = Peltier Element
  T1 = LM35 Temperature Sensor [package="TO92 [THT]"]
  T2 = LM35 Temperature Sensor [package="TO92 [THT]"]
  R1 = Resistor [tolerance=±5% resistance=2.2k package=THT]
  R2 = Resistor [tolerance=±5% resistance=2.2k package=THT]
  U1 = TA7291P [package=HSIP10-P-2.54(THT)]
  VCC1 = Battery 6V
  Q1 = MOSFET-NCHANNEL [package=to220v]
  BAT1 = Battery Holders [package=battcon_245mm]
  U2 = Vibration Motor- ROB-08449 [package=vibe-motor-10mm]

nets:
  N1: パーツ1.A0, T2.Vout, R2.Pin_0
  N2: パーツ1.A1, T1.Vout, R1.Pin_0
  N3: パーツ1.D11_PWM/MOSI, Q1.G
  N4: パーツ1.D2, U1.IN1
  N5: パーツ1.D3_PWM, U1.Vref
  N6: パーツ1.D4, U1.IN2
  5V: パーツ1.5V, R1.Pin_1, R2.Pin_1, U1.Vcc
  GND: パーツ1.GND, T1.GND, T2.GND, U1.GND, VCC1.-, Q1.S, BAT1.-
  N7: J1.pin1, U1.OUT2
  N8: J1.pin2, U1.OUT1
  N9: U1.Vs, VCC1.+
  N10: Q1.D, U2.+
  N11: BAT1.+, U2.-

notes:
  冷却用のDCファン
  外部電源6V
  外部電源12V
  MOSFET

custom parts:
  TA7291P: The IC are Full-Bridge Driver. 4 modes available (CW / CCW / STOP / BRAKE) and PWM control. Output current:1.0 A (AVE.) 2.0 A (PEAK)
  Battery 6V: Your standard 4x AA battery pack (6 Volts)
