# Fritzing sketch Air_Pumps_circuits (saved by Fritzing 0.9.3b)
breadboards: 1

parts:
  パーツ1 = Arduino Uno (Rev3) - ICSP
  VCC1 = Battery 6V
  VCC2 = Battery 6V
  Q2 = MOSFET-NCHANNEL [package=to220v]
  Q3 = MOSFET-NCHANNEL [package=to220v]
  Q4 = MOSFET-NCHANNEL [package=to220v]
  Q5 = MOSFET-NCHANNEL [package=to220v]
  M1 = DC Motor
  M2 = DC Motor
  M3 = DC Motor
  M4 = DC Motor

nets:
  N1: パーツ1.GND, VCC2.-, Q2.S, Q3.S, Q4.S, Q5.S
  N2: パーツ1.D9_PWM, Q5.G
  N3: パーツ1.D3_PWM, Q2.G
  N4: パーツ1.D5_PWM, Q3.G
  N5: パーツ1.D6_PWM, Q4.G
  N6: VCC1.-, VCC2.+
  N7: VCC1.+, M1.pin_2, M2.pin_2, M3.pin_2, M4.pin_2
  N8: Q2.D, M1.pin_1
  N9: Q3.D, M2.pin_1
  N10: Q4.D, M3.pin_1
  N11: Q5.D, M4.pin_1

notes:
  12V電源
  MOSFET K2233 803
  Air Pumps

custom parts:
  Battery 6V: Your standard 4x AA battery pack (6 Volts)
