# Fritzing sketch circuit_peltier_&_sensors (saved by Fritzing 0.9.3b)
breadboards: 2

parts:
  パーツ1 = Arduino Uno (Rev3)
  J1 = Peltier Element
  R1 = Resistor [tolerance=±5% resistance=2.2k package=THT]
  R2 = Resistor [tolerance=±5% resistance=2.2k package=THT]
  U1 = TA7291P [package=HSIP10-P-2.54(THT)]
  VCC1 = Battery 6V
  Q1 = MOSFET-NCHANNEL [package=to220v]
  BAT1 = Battery Holders [package=battcon_245mm]
  U2 = Vibration Motor- ROB-08449 [package=vibe-motor-10mm]
  R3 = Temperature Sensor (Thermistor) [thermistor_type=NTC package=THT]
  R4 = Temperature Sensor (Thermistor) [thermistor_type=NTC package=THT]

nets:
  N1: パーツ1.A0, R2.Pin_0, R3.pin_0
  N2: パーツ1.A1, R1.Pin_0, R4.pin_0
  N3: パーツ1.D11_PWM/MOSI, Q1.G
  N4: パーツ1.D2, U1.IN1
  N5: パーツ1.D3_PWM, U1.Vref
  N6: パーツ1.D4, U1.IN2
  5V: パーツ1.5V, U1.Vcc, R3.pin_1, R4.pin_1
  GND: パーツ1.GND, R1.Pin_1, R2.Pin_1, U1.GND, VCC1.-, Q1.S, BAT1.-
  N7: J1.pin1, U1.OUT2
  N8: J1.pin2, U1.OUT1
  N9: U1.Vs, VCC1.+
  N10: Q1.D, U2.+
  N11: BAT1.+, U2.-

notes:
  [サーミスタ抵抗 4.7KΩ]
  サーミスタは103JT-025
  ファンは12V

custom parts:
  TA7291P: The IC are Full-Bridge Driver. 4 modes available (CW / CCW / STOP / BRAKE) and PWM control. Output current:1.0 A (AVE.) 2.0 A (PEAK)
  Battery 6V: Your standard 4x AA battery pack (6 Volts)
