# Fritzing sketch total_circuits (saved by Fritzing 0.9.3b)
breadboards: 2

parts:
  パーツ2 = Arduino Uno (Rev3)
  ペルチェ素子 = Peltier Element
  U2 = TA7291P [package=HSIP10-P-2.54(THT)]
  外部電源_6V = Battery Holders [package=battcon_245mm]
  KSC1815YTA = TRANSISTOR_NPN [package=to-92]
  part = Resistor [tolerance=±5% resistance=820 package=THT]
  part_2 = Resistor [tolerance=±5% resistance=7.5 package=THT]
  DCファン = Vibration Motor- ROB-08449 [package=vibe-motor-10mm]
  R5 = Temperature Sensor (Thermistor) [thermistor_type=NTC package=THT]
  103JT-025 = Temperature Sensor (Thermistor) [thermistor_type=NTC package=THT]
  R6 = Resistor [tolerance=±5% resistance=4.7k package=THT]
  part_3 = Resistor [tolerance=±5% resistance=4.7k package=THT]
  K2233_803 = MOSFET-NCHANNEL [package=to220v]
  Q7 = MOSFET-NCHANNEL [package=to220v]
  Q8 = MOSFET-NCHANNEL [package=to220v]
  Q9 = MOSFET-NCHANNEL [package=to220v]
  外部電源_12V = Battery Holders [package=battcon_245mm]
  M2 = DC Motor
  M3 = DC Motor
  M4 = DC Motor
  M5 = DC Motor

nets:
  N1: パーツ2.A0, R5.pin_0, R6.Pin_1
  N2: パーツ2.A1, 103JT-025.pin_0, part_3.Pin_1
  N3: パーツ2.D9_PWM, K2233_803.G
  N4: パーツ2.D10_PWM/SS, part.Pin_0
  N5: パーツ2.D11_PWM/MOSI, U2.Vref
  N6: パーツ2.D12/MISO, U2.IN2
  N7: パーツ2.D13/SCK, U2.IN1
  N8: パーツ2.D3_PWM, Q9.G
  N9: パーツ2.D5_PWM, Q8.G
  N10: パーツ2.D6_PWM, Q7.G
  5V: パーツ2.5V, U2.Vcc, R5.pin_1, 103JT-025.pin_1
  N11: ペルチェ素子.pin1, U2.OUT2
  N12: ペルチェ素子.pin2, U2.OUT1
  N13: U2.GND, 外部電源_6V.-, KSC1815YTA.E, R6.Pin_0, part_3.Pin_0, K2233_803.S, Q7.S, Q8.S, Q9.S, 外部電源_12V.-
  N14: U2.Vs, 外部電源_6V.+, part_2.Pin_1
  N15: KSC1815YTA.B, part.Pin_1
  N16: KSC1815YTA.C, DCファン.+
  N17: part_2.Pin_0, DCファン.-
  N18: K2233_803.D, M5.pin_1
  N19: Q7.D, M4.pin_1
  N20: Q8.D, M3.pin_1
  N21: Q9.D, M2.pin_1
  N22: 外部電源_12V.+, M2.pin_2, M3.pin_2, M4.pin_2, M5.pin_2

notes:
  エアポンプ 12V駆動

custom parts:
  TA7291P: The IC are Full-Bridge Driver. 4 modes available (CW / CCW / STOP / BRAKE) and PWM control. Output current:1.0 A (AVE.) 2.0 A (PEAK)
