# Fritzing sketch circuit_peltier_&_sensors (saved by Fritzing 0.9.4)
breadboards: 1

parts:
  パーツ1 = Arduino Uno (Rev3)
  J1 = Peltier Element
  T1 = LM35 Temperature Sensor [package="TO92 [THT]"]
  T2 = LM35 Temperature Sensor [package="TO92 [THT]"]
  R1 = Resistor [tolerance=±5% resistance=2.2k package=THT]
  R2 = Resistor [tolerance=±5% resistance=2.2k package=THT]
  U1 = TA7291P [package=HSIP10-P-2.54(THT)]
  VCC1 = Battery 6V

nets:
  N1: パーツ1.A0, T2.Vout, R2.Pin_0
  N2: パーツ1.A1, T1.Vout, R1.Pin_0
  N3: パーツ1.D0/RX, U1.IN1
  N4: パーツ1.D1/TX, U1.IN2
  N5: パーツ1.D3_PWM, U1.Vref
  5V: パーツ1.5V, R1.Pin_1, R2.Pin_1, U1.Vcc
  GND: パーツ1.GND, T1.GND, T2.GND, U1.GND, VCC1.-
  N6: J1.pin1, U1.OUT2
  N7: J1.pin2, U1.OUT1
  N8: U1.Vs, VCC1.+

custom parts:
  TA7291P: The IC are Full-Bridge Driver. 4 modes available (CW / CCW / STOP / BRAKE) and PWM control. Output current:1.0 A (AVE.) 2.0 A (PEAK)
  Battery 6V: Your standard 4x AA battery pack (6 Volts)
